# Fritzing sketch MPL115A2_RPI (saved by Fritzing 0.9.2b)
breadboards: 1

parts:
  Raspberry_Pi1 = Raspberry Pi 2
  SENSOR1 = MPL115A2 Barometer Breakout Board

nets:
  3V3: Raspberry_Pi1.3v3, SENSOR1.VDD
  N1: Raspberry_Pi1.GPIO2, SENSOR1.SDA
  N2: Raspberry_Pi1.GPIO3, SENSOR1.SCL
  GND: Raspberry_Pi1.GND, SENSOR1.GND

custom parts:
  MPL115A2 Barometer Breakout Board: MPL115A2 I2C Barometric Sensor
